// Logisim project Hazard_detector.circ as structural Verilog: 1 circuit, main circuit main
module main (
  input  [4:0] Rd,
  input  [4:0] Rs,
  input  RegWrite,
  input  [4:0] Rt,
  output out_5
);

  wire and_1_out, and_2_out, comparator_1_eq, comparator_2_eq, comparator_3_eq, comparator_4_eq,
       comparator_5_eq, not_1_out, or_1_out;

  Comparator #(.width(5)) comparator_1 (.a(Rd), .b(Rs), .eq(comparator_1_eq));  // open: gt, lt
  Comparator #(.width(5)) comparator_2 (.a(Rd), .b(Rt), .eq(comparator_2_eq));  // open: gt, lt
  Comparator #(.width(5)) comparator_3 (.a(Rd), .b({5{1'b0}}), .eq(comparator_3_eq));  // open: gt, lt
  Comparator #(.width(5)) comparator_4 (.a(Rs), .b({5{1'b0}}), .eq(comparator_4_eq));  // open: gt, lt
  Comparator #(.width(5)) comparator_5 (.a(Rt), .b({5{1'b0}}), .eq(comparator_5_eq));  // open: gt, lt
  or or_1 (or_1_out, comparator_1_eq, comparator_2_eq);
  and and_1 (and_1_out, comparator_3_eq, comparator_4_eq, comparator_5_eq);
  and and_2 (and_2_out, RegWrite, or_1_out);
  not not_1 (not_1_out, and_1_out);
  and and_3 (out_5, and_2_out, not_1_out);
endmodule
