// Logisim project Pipeline.circ as structural Verilog: 4 circuits, main circuit IF/ID
module IF_ID (
  input  Enable,
  input  [31:0] Inst_IF,
  input  Clock,
  input  Clear,
  input  [23:0] PC_ID,
  output [31:0] Inst_ID,
  output [23:0] PC_IF
);

  Register #(.width(32)) register_1 (.D(Inst_IF), .en(Enable), .Q(Inst_ID), .clk(Clock), .clr(Clear));
  Register #(.width(24)) register_2 (.D(PC_ID), .en(Enable), .Q(PC_IF), .clk(Clock), .clr(Clear));
endmodule

module ID_EX (
  input  Clear,
  input  ALUCtrl3_ID,
  input  [15:0] Imm_ID,
  input  [4:0] Shamt_ID,
  input  ALUCtrl2_ID,
  input  ALUSrc_ID,
  input  [31:0] BusA_ID,
  input  [25:0] JumpAddr,
  input  ALUCtrl1_ID,
  input  MemtoReg_ID,
  input  Clock,
  input  ALUCtrl0_ID,
  input  RegWrite_ID,
  input  [31:0] BusB_ID,
  input  [23:0] PC_ID,
  input  Jump_ID,
  input  MemRead_ID,
  input  MemWrite_ID,
  input  Branch_ID,
  input  Bne_ID,
  input  Enable,
  output ALUCtrl3_EX,
  output [15:0] Imm_EX,
  output [4:0] Shamt_EX,
  output ALUCtrl2_EX,
  output ALUSrc_EX,
  output [31:0] BusA_EX,
  output [25:0] JumpAddr_2,
  output ALUCtrl1_EX,
  output MemtoReg_EX,
  output ALUCtrl0_EX,
  output RegWrite_EX,
  output [31:0] BusB_EX,
  output [23:0] PC_EX,
  output Jump_EX,
  output MemRead_EX,
  output MemWrite_EX,
  output Branch_EX,
  output Bne_EX
);

  Register #(.width(16)) register_1 (.D(Imm_ID), .en(Enable), .Q(Imm_EX), .clk(Clock), .clr(Clear));
  Register #(.width(32)) register_2 (.D(BusA_ID), .en(Enable), .Q(BusA_EX), .clk(Clock), .clr(Clear));
  Register #(.width(32)) register_3 (.D(BusB_ID), .en(Enable), .Q(BusB_EX), .clk(Clock), .clr(Clear));
  Register #(.width(5)) register_4 (.D(Shamt_ID), .en(Enable), .Q(Shamt_EX), .clk(Clock), .clr(Clear));
  Register #(.width(26)) register_5 (.D(JumpAddr), .en(Enable), .Q(JumpAddr_2), .clk(Clock), .clr(Clear));
  Register #(.width(24)) register_6 (.D(PC_ID), .en(Enable), .Q(PC_EX), .clk(Clock), .clr(Clear));
  Register #(.width(1)) register_7 (.D(ALUSrc_ID), .en(Enable), .Q(ALUSrc_EX), .clk(Clock), .clr(Clear));
  Register #(.width(1)) register_8 (.D(MemtoReg_ID), .en(Enable), .Q(MemtoReg_EX), .clk(Clock), .clr(Clear));
  Register #(.width(1)) register_9 (.D(RegWrite_ID), .en(Enable), .Q(RegWrite_EX), .clk(Clock), .clr(Clear));
  Register #(.width(1)) register_10 (.D(MemRead_ID), .en(Enable), .Q(MemRead_EX), .clk(Clock), .clr(Clear));
  Register #(.width(1)) register_11 (.D(MemWrite_ID), .en(Enable), .Q(MemWrite_EX), .clk(Clock), .clr(Clear));
  Register #(.width(1)) register_12 (.D(Branch_ID), .en(Enable), .Q(Branch_EX), .clk(Clock), .clr(Clear));
  Register #(.width(1)) register_13 (.D(Bne_ID), .en(Enable), .Q(Bne_EX), .clk(Clock), .clr(Clear));
  Register #(.width(1)) register_14 (.D(ALUCtrl3_ID), .en(Enable), .Q(ALUCtrl3_EX), .clk(Clock), .clr(Clear));
  Register #(.width(1)) register_15 (.D(ALUCtrl2_ID), .en(Enable), .Q(ALUCtrl2_EX), .clk(Clock), .clr(Clear));
  Register #(.width(1)) register_16 (.D(ALUCtrl1_ID), .en(Enable), .Q(ALUCtrl1_EX), .clk(Clock), .clr(Clear));
  Register #(.width(1)) register_17 (.D(ALUCtrl0_ID), .en(Enable), .Q(ALUCtrl0_EX), .clk(Clock), .clr(Clear));
  Register #(.width(1)) register_18 (.D(Jump_ID), .en(Enable), .Q(Jump_EX), .clk(Clock), .clr(Clear));
endmodule

module EX_MEM (
  input  Clock,
  input  Clear,
  input  MentoReg_EX,
  input  [31:0] ALUResult_EX,
  input  RegWrite_EX,
  input  MemRead_EX,
  input  [23:0] PC_EX,
  input  MemWrite_EX,
  input  [31:0] BusB_EX,
  input  Enable,
  output MentoReg_MEM,
  output [31:0] ALUResult_MEM,
  output RegWrite_MEM,
  output MemRead_MEM,
  output [23:0] PC_MEM,
  output MemWrite_MEM,
  output [31:0] BusB_MEM
);

  Register #(.width(1)) register_1 (.D(MentoReg_EX), .en(Enable), .Q(MentoReg_MEM), .clk(Clock), .clr(Clear));
  Register #(.width(1)) register_2 (.D(RegWrite_EX), .en(Enable), .Q(RegWrite_MEM), .clk(Clock), .clr(Clear));
  Register #(.width(1)) register_3 (.D(MemRead_EX), .en(Enable), .Q(MemRead_MEM), .clk(Clock), .clr(Clear));
  Register #(.width(1)) register_4 (.D(MemWrite_EX), .en(Enable), .Q(MemWrite_MEM), .clk(Clock), .clr(Clear));
  Register #(.width(32)) register_5 (.D(ALUResult_EX), .en(Enable), .Q(ALUResult_MEM), .clk(Clock), .clr(Clear));
  Register #(.width(24)) register_6 (.D(PC_EX), .en(Enable), .Q(PC_MEM), .clk(Clock), .clr(Clear));
  Register #(.width(32)) register_7 (.D(BusB_EX), .en(Enable), .Q(BusB_MEM), .clk(Clock), .clr(Clear));
endmodule

module MEM_WB (
  input  Clock,
  input  Clear,
  input  [31:0] ALUResult_MEM,
  input  MemtoReg_MEM,
  input  RegWriteMEM,
  input  [31:0] BusW_MEM,
  input  MemRead_MEM,
  input  [23:0] PC_MEM,
  input  Enable,
  output [31:0] ALUResult_WB,
  output MemtoReg_WB,
  output RegWriteWB,
  output [31:0] BusW_WB,
  output MemRead_WB,
  output [23:0] PC_WB
);

  Register #(.width(1)) register_1 (.D(MemtoReg_MEM), .en(Enable), .Q(MemtoReg_WB), .clk(Clock), .clr(Clear));
  Register #(.width(1)) register_2 (.D(RegWriteMEM), .en(Enable), .Q(RegWriteWB), .clk(Clock), .clr(Clear));
  Register #(.width(1)) register_3 (.D(MemRead_MEM), .en(Enable), .Q(MemRead_WB), .clk(Clock), .clr(Clear));
  Register #(.width(32)) register_4 (.D(ALUResult_MEM), .en(Enable), .Q(ALUResult_WB), .clk(Clock), .clr(Clear));
  Register #(.width(32)) register_5 (.D(BusW_MEM), .en(Enable), .Q(BusW_WB), .clk(Clock), .clr(Clear));
  Register #(.width(24)) register_6 (.D(PC_MEM), .en(Enable), .Q(PC_WB), .clk(Clock), .clr(Clear));
endmodule
